# Fritzing sketch 3S-Schematic (saved by Fritzing 0.9.9b)
breadboards: 1

parts:
  SW1 = SWITCH-SPST-2 [package=switch-spst-vertical]
  VCC2 = Battery
  VCC3 = Battery
  BMS1 = 3S-BMS
  M1 = RioRand LM2596
  J1 = Power Jack [package=power_jack_pth]
  X1 = USB Connectors [package=usb-b-pth-vertical]
  R1 = Resistor [tolerance=±5% power=0.25 resistance=100k package=THT]
  VM1 = Multimeter (DC Voltage)
  VCC1 = Battery

nets (from the schematic view):
  N1: SW1.O, BMS1.12.6V
  N2: SW1.P, VCC1.-
  N3: VCC2.-, BMS1.8.4V, VCC1.+
  N4: VCC2.+, VCC3.-, BMS1.4.2V
  N5: VCC3.+, BMS1.0V
  N6: BMS1.-, M1.Pin_2, X1.GND, R1.Pin_0
  N7: BMS1.+, M1.Pin_1, X1.D+, R1.Pin_1
  N8: M1.Pin_3, J1.PWR, VM1.V_Probe
  N9: M1.Pin_4, J1.GND, VM1.COM_Probe

custom parts:
  3S-BMS: 3S-BMS LIPO battery charger / protection unit. Note pcb does not match the board as it will likely connect with wires, so pcb is 6 pads suitable for .1in header pins.
